// Logisim project oblig1.circ as structural Verilog: 3 circuits, main circuit main
module main (
  input  [3:0] in_1,
  input  \Negativt_når_1 ,
  output [8:0] out_3
);

  wire [7:0] buffer_inverter_kontrol_1_out_3, buffer_inverter_kontrol_1_out_4, multiplikator_1_y0___0;

  Multiplikator multiplikator_1 (
    .A3(in_1[3]), .A2(in_1[2]), .A1(in_1[1]), .A0(in_1[0]), .Y7___128(multiplikator_1_y0___0[7]),
    .Y6___64(multiplikator_1_y0___0[6]), .Y5___32(multiplikator_1_y0___0[5]),
    .Y4___16(multiplikator_1_y0___0[4]), .Y3___8(multiplikator_1_y0___0[3]),
    .Y2___4(multiplikator_1_y0___0[2]), .Y1___2(multiplikator_1_y0___0[1]), .Y0___0(multiplikator_1_y0___0[0]));
  buffer_Inverter_Kontrol buffer_inverter_kontrol_1 (
    .in_1(multiplikator_1_y0___0), .in_2(\Negativt_når_1 ), .out_3(buffer_inverter_kontrol_1_out_3),
    .out_4(buffer_inverter_kontrol_1_out_4));
  Adder adder_1 (
    .a(buffer_inverter_kontrol_1_out_4), .b(8'h1), .out(buffer_inverter_kontrol_1_out_3));  // open: cin, cout
  assign out_3 = {{1{\Negativt_når_1 }}, buffer_inverter_kontrol_1_out_3};  // Bit_Extender bit_extender_1

  // Notes on the sheet:
  //   Multiplikator
  //   Buffer_Inverter_Kontroll
  //   Legger til 1 bit til LSB
  //   komplimentær bestemmerlsesbit
endmodule

module Multiplikator (
  input  A3,
  input  A2,
  input  A1,
  input  A0,
  output Y7___128,
  output Y6___64,
  output Y5___32,
  output Y4___16,
  output Y3___8,
  output Y2___4,
  output Y1___2,
  output Y0___0
);

  wire and_1_out, and_2_out, and_3_out, and_4_out, and_5_out, and_6_out, and_7_out, and_8_out, and_9_out,
       and_10_out, and_11_out, and_12_out, and_13_out, and_14_out, and_15_out, and_16_out, not_1_out,
       not_2_out, not_3_out, not_4_out, or_1_out;

  not not_1 (not_1_out, A3);
  not not_2 (not_2_out, A1);
  not not_3 (not_3_out, A2);
  not not_4 (not_4_out, A0);
  or or_1 (or_1_out, A0, A1);
  and and_1 (and_1_out, A3, not_3_out);
  and and_2 (and_2_out, A3, not_2_out, not_4_out);
  and and_3 (and_3_out, not_1_out, A2, A1, A0);
  and and_4 (and_4_out, A2, not_2_out, not_4_out);
  and and_5 (and_5_out, not_1_out, A2, not_2_out);
  and and_6 (and_6_out, A3, not_3_out, A1);
  and and_7 (and_7_out, not_1_out, A2, not_4_out);
  and and_8 (and_8_out, not_1_out, not_3_out, A1);
  and and_9 (and_9_out, not_1_out, A1, not_4_out);
  and and_10 (and_10_out, A3, not_2_out, not_4_out);
  and and_11 (and_11_out, A3, not_3_out, not_2_out);
  and and_12 (and_12_out, not_1_out, A2, not_2_out, A0);
  and and_13 (and_13_out, A2, not_4_out);
  and and_14 (and_14_out, not_3_out, A0);
  and and_15 (and_15_out, A3, A2);
  or or_2 (Y6___64, and_1_out, and_2_out, and_3_out);
  or or_3 (Y5___32, and_4_out, and_5_out, and_6_out, and_7_out);
  and and_16 (and_16_out, A3, A2, A1, A0);
  or or_4 (Y3___8, and_13_out, and_14_out);
  and and_17 (Y7___128, and_15_out, or_1_out);
  or or_5 (Y4___16, and_8_out, and_9_out, and_10_out, and_11_out, and_12_out, and_16_out);

  assign Y0___0 = 1'b0;
  assign Y1___2 = A0;
  assign Y2___4 = A1;
endmodule

module buffer_Inverter_Kontrol (
  input  [7:0] in_1,
  input  in_2,
  output [7:0] out_3,
  output [7:0] out_4
);

  wire not_1_out;
  wire [7:0] not_2_out;

  not not_1 (not_1_out, in_2);
  assign out_3 = not_1_out ? in_1 : 8'bz;  // Controlled_Buffer controlled_buffer_1
  assign not_2_out = ~in_1;  // NOT_Gate not_2, 8 bits wide
  assign out_4 = in_2 ? not_2_out : 8'bz;  // Controlled_Buffer controlled_buffer_2
endmodule
