// Logisim project mini_CPU.circ as structural Verilog: 18 circuits, main circuit main
module main (
  input  in_1,
  input  in_2,
  input  in_3,
  input  in_4
);

  wire clock_1_out, data_reg_ctrl_1_ow_select, data_reg_ctrl_1_r_enable, data_reg_ctrl_1_read_enable,
       data_reg_ctrl_1_write_enable, sel_load_ctrl_1_aaaa_enable, sel_load_ctrl_1_dddd_enable,
       sel_load_ctrl_1_load, sel_load_ctrl_1_select;
  wire [3:0] controlled_buffer_1_out, controlled_buffer_2_out, Counter_out_3;
  wire [7:0] d_inn_1_d, ow_ctrl_1_ow_out, R_q, ram_1_data, ram_2_data, read_write_ctrl_1_read_out;

  Counter Counter (.in_1(clock_1_out), .in_2(in_2), .out_3(Counter_out_3));
  Clock clock_1 (.out(clock_1_out));
  RAM #(.addrWidth(4)) ram_1 (
    .addr(Counter_out_3), .data(ram_1_data), .sel(1'b1), .clk(clock_1_out), .ld(1'b1), .clr(in_3));
  assign controlled_buffer_1_out = sel_load_ctrl_1_dddd_enable ? ram_1_data[3:0] : 4'bz;  // Controlled_Buffer controlled_buffer_1
  assign controlled_buffer_2_out = sel_load_ctrl_1_aaaa_enable ? ram_1_data[3:0] : 4'bz;  // Controlled_Buffer controlled_buffer_2
  sel_load_ctrl sel_load_ctrl_1 (
    .DDDD_Enable(sel_load_ctrl_1_dddd_enable), .AAAA_Enable(sel_load_ctrl_1_aaaa_enable),
    .Select(sel_load_ctrl_1_select), .Load(sel_load_ctrl_1_load), .in_1(ram_1_data[7:4]));
  RAM #(.addrWidth(4)) ram_2 (
    .addr(controlled_buffer_2_out), .data(ram_2_data), .sel(sel_load_ctrl_1_select), .clk(clock_1_out),
    .ld(sel_load_ctrl_1_load), .clr(in_1));
  Data_Reg_ctrl data_reg_ctrl_1 (
    .Read_Enable(data_reg_ctrl_1_read_enable), .Write_Enable(data_reg_ctrl_1_write_enable),
    .R_enable(data_reg_ctrl_1_r_enable), .OW_Select(data_reg_ctrl_1_ow_select), .in_1(ram_1_data[7:4]));
  Read_write_Ctrl read_write_ctrl_1 (
    .Write_out(ram_2_data), .Read_inn(ram_2_data), .Read(data_reg_ctrl_1_read_enable),
    .Write(data_reg_ctrl_1_write_enable), .Write_in(R_q), .Read_out(read_write_ctrl_1_read_out));
  OW_Ctrl ow_ctrl_1 (
    .Q(R_q), .DDDD(controlled_buffer_1_out), .OW_Select(data_reg_ctrl_1_ow_select), .OW_out(ow_ctrl_1_ow_out));
  D_inn d_inn_1 (
    .Read_out(read_write_ctrl_1_read_out), .Read_Enable(data_reg_ctrl_1_read_enable), .D(d_inn_1_d),
    .OW_out(ow_ctrl_1_ow_out));
  Register R (.D(d_inn_1_d), .en(data_reg_ctrl_1_r_enable), .Q(R_q), .clk(clock_1_out), .clr(in_4));

  // Notes on the sheet:
  //    Instruksjonsminne
  //   Dataminne
  //   Read / Write
  //   Systembuss
  //   Overskrive CTRL
endmodule

module Read_write_Ctrl (
  input  [7:0] Write_in,
  input  [7:0] Read_inn,
  input  Read,
  input  Write,
  output [7:0] Write_out,
  output [7:0] Read_out
);

  assign Write_out = Write ? Write_in : 8'bz;  // Controlled_Buffer controlled_buffer_1
  assign Read_out = Read ? Read_inn : 8'bz;  // Controlled_Buffer controlled_buffer_2
endmodule

module R_MSB_LSB_CTRL (
  input  [3:0] in_1,
  output out_2
);

  wire not_1_out;

  not not_1 (not_1_out, in_1[0]);
  and and_1 (out_2, in_1[3], in_1[2], in_1[1], not_1_out);
endmodule

module OW_SELECT (
  input  a,
  input  b,
  input  c,
  input  d,
  output x
);

  wire not_1_out, not_2_out;

  not not_1 (not_1_out, b);
  not not_2 (not_2_out, c);
  and and_1 (x, a, not_1_out, not_2_out, d);
endmodule

module Load (
  input  a,
  input  b,
  input  c,
  input  d,
  output x
);

  wire not_1_out, not_2_out;

  not not_1 (not_1_out, b);
  not not_2 (not_2_out, d);
  and and_1 (x, a, not_1_out, c, not_2_out);
endmodule

module Reg_Ctrl (
  input  a,
  input  b,
  input  c,
  input  d,
  output x
);

  wire and_1_out, and_2_out, not_1_out, not_2_out, not_3_out, not_4_out;

  not not_1 (not_1_out, b);
  and and_1 (and_1_out, a, not_1_out, not_2_out);
  not not_2 (not_2_out, c);
  not not_3 (not_3_out, b);
  and and_2 (and_2_out, a, not_3_out, not_4_out);
  not not_4 (not_4_out, d);
  or or_1 (x, and_1_out, and_2_out);
endmodule

module OW_Ctrl (
  input  [7:0] Q,
  input  [3:0] DDDD,
  input  OW_Select,
  output [7:0] OW_out
);

  wire not_1_out, not_2_out, not_3_out;
  wire [3:0] bitselector_1_out;

  BitSelector #(.group(4)) bitselector_1 (.in(Q), .out(bitselector_1_out), .sel(not_1_out));
  not not_1 (not_1_out, OW_Select);
  not not_2 (not_2_out, not_1_out);
  assign OW_out[3:0] = not_1_out ? DDDD : 4'bz;  // Controlled_Buffer controlled_buffer_1
  assign OW_out[7:4] = not_1_out ? bitselector_1_out : 4'bz;  // Controlled_Buffer controlled_buffer_2
  assign OW_out[3:0] = not_3_out ? bitselector_1_out : 4'bz;  // Controlled_Buffer controlled_buffer_3
  not not_3 (not_3_out, not_1_out);
  assign OW_out[7:4] = not_2_out ? DDDD : 4'bz;  // Controlled_Buffer controlled_buffer_4

  // Notes on the sheet:
  //   Select
endmodule

module Counter (
  input  in_1,
  input  in_2,
  output [3:0] out_3
);

  wire adder_1_cout, not_1_out;
  wire [3:0] adder_1_out;

  Adder #(.width(4)) adder_1 (.a(4'b0001), .b(out_3), .out(adder_1_out), .cout(adder_1_cout));  // open: cin
  Register #(.width(4)) register_1 (.D(adder_1_out), .en(not_1_out), .Q(out_3), .clk(in_1), .clr(in_2));
  not not_1 (not_1_out, adder_1_cout);
endmodule

module DR_CTRL (
  input  a,
  input  b,
  input  c,
  input  d,
  output x
);

  wire not_1_out;

  and and_1 (x, a, not_1_out);
  not not_1 (not_1_out, b);
  // also tied to GND on the sheet: {c, d}
endmodule

module Write_enable (
  input  a,
  input  b,
  input  c,
  input  d,
  output x
);

  wire not_1_out;

  not not_1 (not_1_out, b);
  and and_1 (x, a, not_1_out, c, d);
endmodule

module sel_load_ctrl (
  input  [3:0] in_1,
  output DDDD_Enable,
  output AAAA_Enable,
  output Select,
  output Load
);

  DDDD_CTRL dddd_ctrl_1 (.a(in_1[3]), .b(in_1[2]), .c(in_1[1]), .d(in_1[0]), .x(DDDD_Enable));
  AAAA_Enable aaaa_enable_1 (.a(in_1[3]), .b(in_1[2]), .c(in_1[1]), .d(in_1[0]), .x(AAAA_Enable));
  Select_Enable select_enable_1 (.a(in_1[3]), .b(in_1[2]), .c(in_1[1]), .d(in_1[0]), .x(Select));
  Load_enable load_enable_1 (.a(in_1[3]), .b(in_1[2]), .c(in_1[1]), .d(in_1[0]), .x(Load));
endmodule

module Data_Reg_ctrl (
  input  [3:0] in_1,
  output Read_Enable,
  output Write_Enable,
  output R_enable,
  output OW_Select
);

  Decoder #(.select(4)) decoder_1 (
    .out10(Read_Enable), .out11(Write_Enable), .sel(in_1));  // open: out0, out1, out2, out3, out4, out5, out6, out7, out8, out9, out12, out13, out14, out15, en
  R_enable r_enable_1 (.a(in_1[3]), .b(in_1[2]), .c(in_1[1]), .d(in_1[0]), .x(R_enable));
  OW_SELECT ow_select_1 (.a(in_1[3]), .b(in_1[2]), .c(in_1[1]), .d(in_1[0]), .x(OW_Select));
endmodule

module R_enable (
  input  a,
  input  b,
  input  c,
  input  d,
  output x
);

  wire and_1_out, and_2_out, not_1_out, not_2_out, not_3_out, not_4_out;

  not not_1 (not_1_out, b);
  and and_1 (and_1_out, a, not_1_out, not_2_out);
  not not_2 (not_2_out, c);
  not not_3 (not_3_out, b);
  and and_2 (and_2_out, a, not_3_out, not_4_out);
  not not_4 (not_4_out, d);
  or or_1 (x, and_1_out, and_2_out);
endmodule

module Load_enable (
  input  a,
  input  b,
  input  c,
  input  d,
  output x
);

  wire and_1_out, and_2_out, not_1_out, not_2_out, not_3_out, not_4_out;

  not not_1 (not_1_out, b);
  and and_1 (and_1_out, a, not_1_out, not_2_out);
  not not_2 (not_2_out, c);
  not not_3 (not_3_out, b);
  and and_2 (and_2_out, a, not_3_out, not_4_out);
  not not_4 (not_4_out, d);
  or or_1 (x, and_1_out, and_2_out);
endmodule

module DDDD_CTRL (
  input  a,
  input  b,
  input  c,
  input  d,
  output x
);

  wire not_1_out, not_2_out;

  and and_1 (x, a, not_1_out, not_2_out);
  not not_1 (not_1_out, b);
  not not_2 (not_2_out, c);
endmodule

module Select_Enable (
  input  a,
  input  b,
  input  c,
  input  d,
  output x
);

  wire not_1_out;

  and and_1 (x, a, not_1_out, c);
  not not_1 (not_1_out, b);
endmodule

module AAAA_Enable (
  input  a,
  input  b,
  input  c,
  input  d,
  output x
);

  wire not_1_out;

  and and_1 (x, a, not_1_out, c);
  not not_1 (not_1_out, b);
endmodule

module D_inn (
  input  [7:0] OW_out,
  input  [7:0] Read_out,
  input  Read_Enable,
  output [7:0] D
);

  wire not_1_out;

  not not_1 (not_1_out, Read_Enable);
  assign D = not_1_out ? OW_out : 8'bz;  // Controlled_Buffer controlled_buffer_1
  assign D = Read_Enable ? Read_out : 8'bz;  // Controlled_Buffer controlled_buffer_2
endmodule
